# Fritzing sketch midiwanne (saved by Fritzing 0.8.7b)
breadboards: 1

parts:
  Arduino1 = Arduino Uno (Rev3)
  S1 = Pushbutton [package="[THT]"]
  S2 = Pushbutton [package="[THT]"]
  S3 = Pushbutton [package="[THT]"]
  S4 = Pushbutton [package="[THT]"]
  S5 = Pushbutton [package="[THT]"]
  S6 = Pushbutton [package="[THT]"]
  S8 = Pushbutton [package="[THT]"]
  S9 = Pushbutton [package="[THT]"]
  S7 = Pushbutton [package="[THT]"]

nets:
  N1: Arduino1.D8, S7.Pin_1, S7.Pin_2
  N2: Arduino1.D9_PWM, S8.Pin_1, S8.Pin_2
  N3: Arduino1.D10_PWM/SS, S9.Pin_1, S9.Pin_2
  N4: Arduino1.GND, S1.Pin_3, S1.Pin_4, S2.Pin_3, S2.Pin_4, S3.Pin_3, S3.Pin_4, S4.Pin_3, S4.Pin_4, S5.Pin_3, S5.Pin_4, S6.Pin_3, S6.Pin_4, S8.Pin_3, S8.Pin_4, S9.Pin_3, S9.Pin_4, S7.Pin_3, S7.Pin_4
  N5: Arduino1.D2, S1.Pin_1, S1.Pin_2
  N6: Arduino1.D3_PWM, S2.Pin_1, S2.Pin_2
  N7: Arduino1.D4, S3.Pin_1, S3.Pin_2
  N8: Arduino1.D5_PWM, S4.Pin_1, S4.Pin_2
  N9: Arduino1.D6_PWM, S5.Pin_1, S5.Pin_2
  N10: Arduino1.D7, S6.Pin_1, S6.Pin_2

notes:
  In this example, groups of three push buttons are used as switches against the internal pullup of the Arduino board. The code on the arduino then transforms the button pushes into MIDI signals (different pitches per group, different velocities within groups).
  The Arduino code can be found here: https://github.com/muthesius/midiwanne

// code stored in the sketch: Button.ino
/*
  Button
 
 Turns on and off a light emitting diode(LED) connected to digital  
 pin 13, when pressing a pushbutton attached to pin 2. 
 
 
 The circuit:
 * LED attached from pin 13 to ground 
 * pushbutton attached to pin 2 from +5V
 * 10K resistor attached to pin 2 from ground
 
 * Note: on most Arduinos there is already an LED on the board
 attached to pin 13.
 
 
 created 2005
 by DojoDave <http://www.0j0.org>
 modified 30 Aug 2011
 by Tom Igoe
 
 This example code is in the public domain.
 
 http://www.arduino.cc/en/Tutorial/Button
 */

// constants won't change. They're used here to 
// set pin numbers:
const int buttonPin = 2;     // the number of the pushbutton pin
const int ledPin =  13;      // the number of the LED pin

// variables will change:
int buttonState = 0;         // variable for reading the pushbutton status

void setup() {
  // initialize the LED pin as an output:
  pinMode(ledPin, OUTPUT);      
  // initialize the pushbutton pin as an input:
  pinMode(buttonPin, INPUT);     
}

void loop(){
  // read the state of the pushbutton value:
  buttonState = digitalRead(buttonPin);

  // check if the pushbutton is pressed.
  // if it is, the buttonState is HIGH:
  if (buttonState == HIGH) {     
    // turn LED on:    
    digitalWrite(ledPin, HIGH);  
  } 
  else {
    // turn LED off:
    digitalWrite(ledPin, LOW); 
  }
}
